# Fritzing sketch keypad (saved by Fritzing 0.9.3b)

parts:
  Part1 = 4x4 Keypad [part_number=101207]
  Raspberry_Pi_1 = Raspberry Pi 3 [part_number=RPI-3-V1.2]

nets:
  N1: Part1.1, Raspberry_Pi_1.GIPO21
  N2: Part1.2, Raspberry_Pi_1.GIPO20
  N3: Part1.3, Raspberry_Pi_1.GIPO16
  N4: Part1.4, Raspberry_Pi_1.GIPO12
  N5: Part1.5, Raspberry_Pi_1.GIPO26
  N6: Part1.6, Raspberry_Pi_1.GIPO19
  N7: Part1.7, Raspberry_Pi_1.GIPO13
  N8: Part1.8, Raspberry_Pi_1.GIPO6

notes:
  M.Javad NajafiRad

custom parts:
  4x4 Keypad: Matrix membrane keypad 4x4
